# Fritzing sketch myTimer-schematic (saved by Fritzing 0.9.3b)

parts:
  Part1 = Adafruit Trinket 5V
  Part2 = 16 NeoPixel Ring [part_number=1463]
  S1 = Pushbutton [package="[THT]"]
  R2 = Rotary Potentiometer (Small) [package=THT]

nets:
  GND: Part1.GND, Part2.GND, S1.Pin_1, S1.Pin_2, R2.leg1
  N1: Part1.#2, R2.wiper
  N2: Part1.#0, Part2.IN
  N3: Part1.#3, S1.Pin_3, S1.Pin_4
  +5V: Part1.+5V, Part2.VDD, R2.leg2

custom parts:
  Adafruit Trinket 5V: Trinket may be small, but do not be fooled by its size! It's a tiny microcontroller board, built around the Atmel ATtiny85, a little chip with a lot of power. We wanted to design a microcontroller board that was small enough to fit into any project, and low cost enough to use without hesitation. Perfect for when you don't want to give up your expensive dev-board and you aren't willing to take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
  16 NeoPixel Ring: 16 ultra bright smart LED NeoPixels are arranged in a circle with 1.75" (44.5mm) outer diameter. The rings are 'chainable' - connect the output pin of one to the input pin of another. Use only one microcontroller pin to control as many as you can chain together! Each LED is addressable as the driver chip is inside the LED. Each one has ~18mA constant current drive so the color will be very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
  Rotary Potentiometer (Small): A rotary adjustable resistor (potentiometer).
